# Fritzing sketch candy1 (saved by Fritzing 0.9.3b)
breadboards: 1

parts:
  J1 = Basic Servo
  Part1 = Arduino Uno (Rev3)
  LED1 = LED - 5mm [color="Red (633nm)" package="5 mm [THT]"]
  VCC2 = Battery
  HC-SR04_Sensor_1 = HC-SR04 Ultrasonic Distance Sensor

nets:
  GND: J1.gnd, Part1.GND, LED1.cathode, VCC2.-, HC-SR04_Sensor_1.GND
  VCC: J1.vcc, Part1.5V, VCC2.+, HC-SR04_Sensor_1.VCC
  N1: J1.pulse, Part1.D13/SCK
  N2: Part1.D10_PWM/SS, LED1.anode
  N3: Part1.D11_PWM/MOSI, HC-SR04_Sensor_1.ECHO
  N4: Part1.D12/MISO, HC-SR04_Sensor_1.TRIG

notes:
  idk maybe i should add resistor for the LED or not.
